# Fritzing sketch DEVR (saved by Fritzing 0.9.3b)
breadboards: 1

parts:
  Parça1 = Arduino Nano (Rev3.0)
  R1 = Photocell (LDR) [package=THT]
  DHT1 = DHT11 Humitidy and Temperature Sensor
  Parça2 = FC-28 Soil Hygrometer Module
  J1 = Basic Servo
  U1 = LIPO-110mAh [package=lipo-110]
  J2 = Piezo Speaker
  R2 = Resistor [tolerance=±5% resistance=10k package=THT]
  R3 = Resistor [tolerance=±5% resistance=10k package=THT]

nets:
  GND: Parça1.GND, DHT1.GND, Parça2.GND, J1.gnd, U1.-, J2.pin1, R2.Pin_0
  N1: Parça1.D2, DHT1.DATA, R3.Pin_1
  N2: Parça1.D3, J1.pulse
  N3: Parça1.D11/MOSI, J2.pin2
  N4: Parça1.VIN, U1.+
  VCC: Parça1.5V, R1.pin_1, DHT1.VDD, Parça2.VCC, J1.vcc, R3.Pin_0
  N5: Parça1.A7, R1.pin_0, R2.Pin_1
  N6: Parça1.A6, Parça2.AO

custom parts:
  DHT11 Humitidy and Temperature Sensor: DHT11 Humidity and Temperature Sensor
  FC-28 Soil Hygrometer Module: The FC-28 is a soil hygrometer module that uses the Texas Instruments LM393 comparator chip to provide an analog measurement of soil humidity. The digital output is high when soil moisture is over a certain threshold, as determined by adjusting the potentiometer.
